// Logisim project Tarefa 3.circ as structural Verilog: 1 circuit, main circuit main
module main (
  input  in_1,
  input  in_2,
  input  [2:0] in_3,
  input  [7:0] in_4,
  input  in_5,
  input  [7:0] in_6
);

  wire clock_1_out, decoder_1_out0, decoder_1_out1;
  wire [6:0] keyboard_1_data;
  wire [7:0] register_1_q;

  Decoder #(.select(3)) decoder_1 (
    .out0(decoder_1_out0), .out1(decoder_1_out1), .sel(in_3), .en(in_2));  // open: out2, out3, out4, out5, out6, out7
  Clock clock_1 (.out(clock_1_out));
  assign in_6 = in_5 ? in_4 : 8'bz;  // Controlled_Buffer controlled_buffer_1
  Register register_1 (.D(in_6), .en(decoder_1_out0), .Q(register_1_q), .clk(clock_1_out));  // open: clr
  DotMatrix #(.matrixcols(8), .matrixrows(1)) dotmatrix_1 (
    .col0(register_1_q[0]), .col1(register_1_q[1]), .col2(register_1_q[2]), .col3(register_1_q[3]),
    .col4(register_1_q[4]), .col5(register_1_q[5]), .col6(register_1_q[6]), .col7(register_1_q[7]));
  Keyboard keyboard_1 (.clk(clock_1_out), .re(decoder_1_out1), .clr(in_2), .data(keyboard_1_data));  // open: avail
  assign in_6 = decoder_1_out1 ? {keyboard_1_data, in_1} : 8'bz;  // Controlled_Buffer controlled_buffer_2
endmodule
